# Fritzing sketch irCanon (saved by Fritzing 0.8.7b)
breadboards: 1

parts:
  Part1 = Arduino Uno (Rev3)
  Part2 = Max Power IR LED Kit
  S1 = Pushbutton [package="[THT]"]
  R1 = Resistor [tolerance=±5% resistance=330 package=THT]

nets:
  N1: Part1.D10_PWM/SS, Part2.CONTROL
  N2: Part1.D12/MISO, S1.Pin_3, S1.Pin_4, R1.Pin_1
  5V: Part1.5V, Part2.VCC, S1.Pin_1, S1.Pin_2
  GND: Part1.GND, Part2.GND, R1.Pin_0
